# Fritzing sketch raspduino (saved by Fritzing 0.8.3b)

parts:
  Part1 = Arduino Uno (Rev3)
  LED1 = LED - 5mm [color="Green (555nm)" package="5 mm [THT]"]

nets:
  N1: Part1.ICSP_SCK, Part1.D13/SCK, LED1.anode
  N2: Part1.GND, LED1.cathode
